# Fritzing sketch schema (saved by Fritzing 1.0.2b)
breadboards: 1

parts:
  LED2 = LED - 3mm [color="Red (633nm)" current=0.030 package="3 mm [THT]"]
  LED3 = LED - 3mm [color="Red (633nm)" current=0.030 package="3 mm [THT]"]
  LED4 = LED - 3mm [color="Yellow (595nm)" current=0.030 package="3 mm [THT]"]
  R3 = Resistor [tolerance=±5% resistance=470 power=0.25 package=THT]
  R4 = Resistor [tolerance=±5% resistance=470 power=0.25 package=THT]
  Mod1 = Passive Buzzer
  BAT1 = LIPO-110mAh [package=lipo-110]
  ISP = Header 5x2 [package=avr_icsp]
  RE1 = KY-040 Rotary encoder [package="Breakout board"]
  Mod2 = 2S-BMS
  XTAL1 = CRYSTAL - kHz [frequency="32 kHz"]
  U1 = atmega328 [package=dip]
  Part1 = FTDI Basic Programmer
  U2 = MAX7219 [package=dil24]
  Disp1 = 20mm 8x8 dot matrix row cathode led display with narrow pcb pads
  R5 = Resistor [tolerance=±5% power=0.25W resistance=10k package=THT]
  R2 = Resistor [tolerance=±5% power=0.25 resistance=470 package=THT]
  R6 = Resistor [tolerance=±5% power=0.25W resistance=2.2k package=THT]
  R7 = Resistor [tolerance=±5% power=0.25W resistance=2.2k package=THT]
  R8 = Resistor [tolerance=±5% power=0.25W resistance=2.2k package=THT]
  C1 = Ceramic Capacitor [capacitance=68nF voltage=35V package="100 mil [THT, multilayer]"]
  C2 = Ceramic Capacitor [capacitance=68nF voltage=35V package="100 mil [THT, multilayer]"]
  C3 = Ceramic Capacitor [capacitance=68nF voltage=35V package="100 mil [THT, multilayer]"]

nets:
  N1: LED2.cathode, R2.Pin_1
  5V/VCC: LED2.anode, LED3.anode, LED4.anode, ISP.2, RE1.Vcc, Mod2.pin3#3, U1.VCC, U1.AVCC, U1.AREF, U2.VCC, R5.Pin_0
  N2: LED3.cathode, R3.Pin_1
  N3: LED4.cathode, R4.Pin_1
  N4: R3.Pin_0, U1.A1
  N5: R4.Pin_0, U1.A2
  N6: Mod1.S, Mod1.NC, U1.D9_(PWM)
  N7: Mod1.-, U1.D10_(PWM)
  N8: BAT1.+, Mod2.pin1
  N9: BAT1.-, Mod2.pin2
  N10: ISP.1, U1.D11_(PWM)
  GND: ISP.4, ISP.6, ISP.8, ISP.10, RE1.GND, Mod2.pin3#2, U1.GND, Part1.GND, U2.GND, U2.GND2, C1.1, C2.1, C3.1
  N11: ISP.5, U1.RESET
  N12: ISP.7, U1.D13
  N13: ISP.9, U1.D12
  N14: RE1.SW, R6.Pin_0
  N15: RE1.DT, R7.Pin_0
  N16: RE1.CLK, R8.Pin_0
  N17: XTAL1.pin_0, U1.XLAT1
  N18: XTAL1.pin_1, U1.XLAT2
  N19: U1.D0_(RX), Part1.TXO
  N20: U1.D1_(TX), Part1.RXI
  N21: U1.D2, R8.Pin_1, C3.0
  N22: U1.D3_(PWM), R7.Pin_1, C2.0
  N23: U1.D4, R6.Pin_1, C1.0
  N24: U1.D5_(PWM), U2.CLK
  N25: U1.D6_(PWM), U2.LOAD
  N26: U1.D7, U2.DIN
  N27: U1.A0, R2.Pin_0
  N28: U2.DIG0, Disp1.pin_9
  N29: U2.DIG4, Disp1.pin_1
  N30: U2.DIG6, Disp1.pin_2
  N31: U2.DIG2, Disp1.pin_8
  N32: U2.DIG3, Disp1.pin_12
  N33: U2.DIG7, Disp1.pin_5
  N34: U2.DIG5, Disp1.pin_7
  N35: U2.DIG1, Disp1.pin_14
  N36: U2.SEGA, Disp1.pin_15
  N37: U2.SEGF, Disp1.pin_3
  N38: U2.SEGB, Disp1.pin_11
  N39: U2.SEGG, Disp1.pin_13
  N40: U2.ISET, R5.Pin_1
  N41: U2.SEGC, Disp1.pin_6
  N42: U2.SEGE, Disp1.pin_4
  N43: U2.SEGDP, Disp1.pin_16
  N44: U2.SEGD, Disp1.pin_10

notes:
  Test LEDs
  Programmer
  Audio out
  Rotary encoder
  BMS
  Debug UART
  LED matrix

custom parts:
  KY-040 Rotary encoder: KY-040 Rotary Encoder with switch on breakout borad from AZ Delivery
  2S-BMS: 2S-BMS LIPO battery charger / protection unit. Note pcb does not match the board as it will likely connect with wires, so pcb is 5 pads suitable for .1in header pins.
